# Fritzing sketch Arduino based (saved by Fritzing 0.7.4b)
breadboards: 1

parts:
  Arduino1 = Arduino
  I2C1 = RJ12
  I2C2 = RJ12
  I2C3 = RJ12
  I2C4 = RJ12
  I2C5 = RJ12
  I2C6 = RJ12
  R1 = Resistor [tolerance=±5% resistance=2k package=THT]
  R2 = Resistor [tolerance=±5% resistance=2k package=THT]
  R3 = Resistor [tolerance=±5% resistance=2k package=THT]
  R4 = Resistor [tolerance=±5% resistance=2k package=THT]
  R5 = Resistor [tolerance=±5% resistance=2k package=THT]
  R6 = Resistor [tolerance=±5% resistance=2k package=THT]
  R7 = Resistor [tolerance=±5% resistance=2k package=THT]
  R8 = Resistor [tolerance=±5% resistance=2k package=THT]
  R9 = Resistor [tolerance=±5% resistance=2k package=THT]
  R10 = Resistor [tolerance=±5% resistance=2k package=THT]
  R11 = Resistor [tolerance=±5% resistance=2k package=THT]
  R12 = Resistor [tolerance=±5% resistance=2k package=THT]

nets:
  GND: Arduino1.GND, I2C1.pin_2, I2C2.pin_2, I2C3.pin_2, I2C4.pin_2, I2C5.pin_2, I2C6.pin_2
  5V: Arduino1.+5V, I2C1.pin_5, I2C2.pin_5, I2C3.pin_5, I2C4.pin_5, I2C5.pin_5, I2C6.pin_5, R1.Pin_1, R2.Pin_1, R3.Pin_1, R4.Pin_1, R5.Pin_1, R6.Pin_1, R7.Pin_1, R8.Pin_1, R9.Pin_1, R10.Pin_1, R11.Pin_1, R12.Pin_1
  N1: I2C1.pin_3, R2.Pin_0
  N2: I2C1.pin_4, R1.Pin_0
  N3: I2C2.pin_3, R3.Pin_0
  N4: I2C2.pin_4, R4.Pin_0
  N5: I2C3.pin_3, R7.Pin_0
  N6: I2C3.pin_4, R8.Pin_0
  N7: I2C4.pin_3, R6.Pin_0
  N8: I2C4.pin_4, R5.Pin_0
  N9: I2C5.pin_3, R11.Pin_0
  N10: I2C5.pin_4, R12.Pin_0
  N11: I2C6.pin_3, R10.Pin_0
  N12: I2C6.pin_4, R9.Pin_0
